// Logisim project Ekran.circ as structural Verilog: 1 circuit, main circuit main
module main (
  input  [3:0] in_1,
  input  [3:0] in_2,
  input  [3:0] in_3
);

  wire clock_1_out, counter_1_carry, keyboard_1_avail, main_2_out_3, main_2_out_5, main_2_out_6, not_1_out,
       register_1_q;
  wire [4:0] main_1_out_2, main_1_out_3, main_2_out_4;
  wire [6:0] keyboard_1_data;
  wire [19:0] main_3_out_5, main_3_out_6, main_3_out_7, main_3_out_8, main_3_out_9, main_3_out_10,
       main_3_out_11, main_3_out_12, main_3_out_13, main_3_out_14, main_3_out_15, main_3_out_16,
       main_3_out_17, main_3_out_18, main_3_out_19, main_3_out_20, main_3_out_21, main_3_out_22,
       main_3_out_23, main_3_out_24, main_4_out_41, main_4_out_42, main_4_out_43, main_4_out_44,
       main_4_out_45, main_4_out_46, main_4_out_47, main_4_out_48, main_4_out_49, main_4_out_50,
       main_4_out_51, main_4_out_52, main_4_out_53, main_4_out_54, main_4_out_55, main_4_out_56,
       main_4_out_57, main_4_out_58, main_4_out_59, main_4_out_60, main_5_outy0, main_5_outy0_2,
       main_5_outy0_3, main_5_outy0_4, main_5_outy0_5, main_5_outy0_6, main_5_outy0_7, main_5_outy0_8,
       main_5_outy0_9, main_5_outy0_10, main_5_outy0_11, main_5_outy0_12, main_5_outy0_13, main_5_outy0_14,
       main_5_outy0_15, main_5_outy0_16, main_5_outy0_17, main_5_outy0_18, main_5_outy18, main_5_outy19,
       shifter_1_out, shifter_2_out, shifter_3_out;

  Keyboard #(.buflen(1)) keyboard_1 (
    .re(1'b1), .clr(keyboard_1_avail), .avail(keyboard_1_avail), .data(keyboard_1_data));  // open: clk
  Clock clock_1 (.out(clock_1_out));
  Counter #(.max('h1e)) counter_1 (.carry(counter_1_carry), .clk(clock_1_out));  // open: load, D, count, Q, clr
  LR_main main_1 (.in_1(keyboard_1_data), .out_2(main_1_out_2), .out_3(main_1_out_3));
  Enter_Up_Down_main main_2 (
    .in_1(keyboard_1_data), .out_4(main_2_out_4), .out_5(main_2_out_5), .out_6(main_2_out_6),
    .in_2(clock_1_out), .out_3(main_2_out_3));
  Counter counter_2 (.clk(counter_1_carry));  // open: load, D, count, Q, carry, clr
  not not_1 (not_1_out, main_2_out_6);
  Shifter #(.width(20)) shifter_1 (.in(20'h200), .\dist (main_1_out_2), .out(shifter_1_out));
  Register #(.width(1), .trigger("high")) register_1 (
    .D(clock_1_out), .Q(register_1_q), .clk(not_1_out), .clr(main_2_out_6));  // open: en
  Shifter #(.width(20), .shift("lr")) shifter_2 (.in(shifter_1_out), .\dist (main_1_out_3), .out(shifter_2_out));
  Shifter #(.width(20), .shift("lr")) shifter_3 (.in(20'h80000), .\dist (main_2_out_4), .out(shifter_3_out));
  Uu_Down32_main main_3 (
    .in_1(main_2_out_4), .in_2(shifter_2_out), .out_5(main_3_out_5), .out_6(main_3_out_6),
    .out_7(main_3_out_7), .out_8(main_3_out_8), .out_9(main_3_out_9), .out_10(main_3_out_10),
    .out_11(main_3_out_11), .out_12(main_3_out_12), .out_13(main_3_out_13), .out_14(main_3_out_14),
    .out_15(main_3_out_15), .out_16(main_3_out_16), .out_17(main_3_out_17), .out_18(main_3_out_18),
    .out_19(main_3_out_19), .out_20(main_3_out_20), .out_21(main_3_out_21), .out_22(main_3_out_22),
    .out_23(main_3_out_23), .out_24(main_3_out_24), .in_3(register_1_q), .in_4(main_2_out_6));
  Register32x32_main main_4 (
    .in_1(main_3_out_5), .in_2(main_3_out_6), .in_3(main_3_out_7), .in_4(main_3_out_8), .in_5(main_3_out_9),
    .in_6(main_3_out_10), .in_7(main_3_out_11), .in_8(main_3_out_12), .in_9(main_3_out_13),
    .in_10(main_3_out_14), .in_11(main_3_out_15), .in_12(main_3_out_16), .in_13(main_3_out_17),
    .in_14(main_3_out_18), .in_15(main_3_out_19), .in_16(main_3_out_20), .in_17(main_3_out_21),
    .in_18(main_3_out_22), .in_19(main_3_out_23), .in_20(main_3_out_24), .out_41(main_4_out_41),
    .out_42(main_4_out_42), .out_43(main_4_out_43), .out_44(main_4_out_44), .out_45(main_4_out_45),
    .out_46(main_4_out_46), .out_47(main_4_out_47), .out_48(main_4_out_48), .out_49(main_4_out_49),
    .out_50(main_4_out_50), .out_51(main_4_out_51), .out_52(main_4_out_52), .out_53(main_4_out_53),
    .out_54(main_4_out_54), .out_55(main_4_out_55), .out_56(main_4_out_56), .out_57(main_4_out_57),
    .out_58(main_4_out_58), .out_59(main_4_out_59), .out_60(main_4_out_60), .in_21(main_5_outy0),
    .in_22(main_5_outy0_2), .in_23(main_5_outy0_3), .in_24(main_5_outy0_4), .in_25(main_5_outy0_5),
    .in_26(main_5_outy0_6), .in_27(main_5_outy0_7), .in_28(main_5_outy0_8), .in_29(main_5_outy0_9),
    .in_30(main_5_outy0_10), .in_31(main_5_outy0_11), .in_32(main_5_outy0_12), .in_33(main_5_outy0_13),
    .in_34(main_5_outy0_14), .in_35(main_5_outy0_15), .in_36(main_5_outy0_16), .in_37(main_5_outy0_17),
    .in_38(main_5_outy0_18), .in_39(main_5_outy18), .in_40(main_5_outy19));
  DotMatrix #(.inputtype("row"), .matrixcols(20), .matrixrows(20)) dotmatrix_1 (
    .row0(main_4_out_41), .row1(main_4_out_42), .row2(main_4_out_43), .row3(main_4_out_44),
    .row4(main_4_out_45), .row5(main_4_out_46), .row6(main_4_out_47), .row7(main_4_out_48),
    .row8(main_4_out_49), .row9(main_4_out_50), .row10(main_4_out_51), .row11(main_4_out_52),
    .row12(main_4_out_53), .row13(main_4_out_54), .row14(main_4_out_55), .row15(main_4_out_56),
    .row16(main_4_out_57), .row17(main_4_out_58), .row18(main_4_out_59), .row19(main_4_out_60));
  Modol_Obliczeniowy_20x20_main main_5 (
    .if_x_in_die(in_1), .if_x_n_born(in_2), .if_x_in_die_2(in_3), .Reset(main_2_out_5),
    .CLK(counter_1_carry), .CLK_Enabler(main_2_out_6), .Overwrite(main_2_out_3), .X(shifter_2_out),
    .Y(shifter_3_out), .OutY0(main_5_outy0), .OutY0_2(main_5_outy0_2), .OutY0_3(main_5_outy0_3),
    .OutY0_4(main_5_outy0_4), .OutY0_5(main_5_outy0_5), .OutY0_6(main_5_outy0_6), .OutY0_7(main_5_outy0_7),
    .OutY0_8(main_5_outy0_8), .OutY0_9(main_5_outy0_9), .OutY0_10(main_5_outy0_10),
    .OutY0_11(main_5_outy0_11), .OutY0_12(main_5_outy0_12), .OutY0_13(main_5_outy0_13),
    .OutY0_14(main_5_outy0_14), .OutY0_15(main_5_outy0_15), .OutY0_16(main_5_outy0_16),
    .OutY0_17(main_5_outy0_17), .OutY0_18(main_5_outy0_18), .OutY18(main_5_outy18), .OutY19(main_5_outy19));
endmodule
