// Logisim project Enter_Up_Down.circ as structural Verilog: 1 circuit, main circuit main
module main (
  input  [6:0] in_1,
  output out_2,
  output [4:0] out_3,
  output out_4
);

  wire and_1_out, comparator_2_eq, comparator_3_eq, comparator_5_gt, comparator_5_lt, or_1_out, or_2_out;

  Comparator #(.width(7)) comparator_1 (.a(in_1), .b(7'b0001010), .eq(out_2));  // open: gt, lt
  Comparator #(.width(7)) comparator_2 (.a(in_1), .b(7'b1110111), .eq(comparator_2_eq));  // open: gt, lt
  Comparator #(.width(7)) comparator_3 (.a(in_1), .b(7'b1110011), .eq(comparator_3_eq));  // open: gt, lt
  Comparator #(.width(7)) comparator_4 (.a(in_1), .b(7'b1110010), .eq(out_4));  // open: gt, lt
  and and_1 (and_1_out, comparator_3_eq, or_2_out);
  Counter #(.width(5), .max('h13), .ongoal("stay")) counter_1 (
    .load(comparator_3_eq), .count(1'b1), .Q(out_3), .clk(or_1_out));  // open: D, carry, clr
  or or_1 (or_1_out, comparator_2_eq, and_1_out);
  or or_2 (or_2_out, comparator_5_gt, comparator_5_lt);
  Comparator #(.width(5)) comparator_5 (
    .a(out_3), .b({5{1'b0}}), .gt(comparator_5_gt), .lt(comparator_5_lt));  // open: eq
endmodule
