// Logisim project Register32x32.circ as structural Verilog: 1 circuit, main circuit main
module main (
  input  in_1,
  input  [31:0] in_2,
  input  [31:0] in_3,
  input  [31:0] in_4,
  input  [31:0] in_5,
  input  [31:0] in_6,
  input  [31:0] in_7,
  input  [31:0] in_8,
  input  [31:0] in_9,
  input  [31:0] in_10,
  input  [31:0] in_11,
  input  [31:0] in_12,
  input  [31:0] in_13,
  input  [31:0] in_14,
  input  [31:0] in_15,
  input  [31:0] in_16,
  input  [31:0] in_17,
  input  [31:0] in_18,
  input  [31:0] in_19,
  input  [31:0] in_20,
  input  [31:0] in_21,
  input  [31:0] in_22,
  input  [31:0] in_23,
  input  [31:0] in_24,
  input  [31:0] in_25,
  input  [31:0] in_26,
  input  [31:0] in_27,
  input  [31:0] in_28,
  input  [31:0] in_29,
  input  [31:0] in_30,
  input  [31:0] in_31,
  input  [31:0] in_32,
  input  [31:0] in_33,
  input  in_34,
  output [31:0] out_35,
  output [31:0] out_36,
  output [31:0] out_37,
  output [31:0] out_38,
  output [31:0] out_39,
  output [31:0] out_40,
  output [31:0] out_41,
  output [31:0] out_42,
  output [31:0] out_43,
  output [31:0] out_44,
  output [31:0] out_45,
  output [31:0] out_46,
  output [31:0] out_47,
  output [31:0] out_48,
  output [31:0] out_49,
  output [31:0] out_50,
  output [31:0] out_51,
  output [31:0] out_52,
  output [31:0] out_53,
  output [31:0] out_54,
  output [31:0] out_55,
  output [31:0] out_56,
  output [31:0] out_57,
  output [31:0] out_58,
  output [31:0] out_59,
  output [31:0] out_60,
  output [31:0] out_61,
  output [31:0] out_62,
  output [31:0] out_63,
  output [31:0] out_64,
  output [31:0] out_65,
  output [31:0] out_66
);

  Register1x32_main main_1 (.in_1(in_2), .in_3(in_1), .out_4(out_35), .in_2(in_34));
  Register1x32_main main_2 (.in_1(in_8), .in_3(in_1), .out_4(out_36), .in_2(in_34));
  Register1x32_main main_3 (.in_1(in_14), .in_3(in_1), .out_4(out_37), .in_2(in_34));
  Register1x32_main main_4 (.in_1(in_20), .in_3(in_1), .out_4(out_38), .in_2(in_34));
  Register1x32_main main_5 (.in_1(in_7), .in_3(in_1), .out_4(out_39), .in_2(in_34));
  Register1x32_main main_6 (.in_1(in_13), .in_3(in_1), .out_4(out_40), .in_2(in_34));
  Register1x32_main main_7 (.in_1(in_19), .in_3(in_1), .out_4(out_41), .in_2(in_34));
  Register1x32_main main_8 (.in_1(in_25), .in_3(in_1), .out_4(out_42), .in_2(in_34));
  Register1x32_main main_9 (.in_1(in_24), .in_3(in_1), .out_4(out_43), .in_2(in_34));
  Register1x32_main main_10 (.in_1(in_18), .in_3(in_1), .out_4(out_44), .in_2(in_34));
  Register1x32_main main_11 (.in_1(in_12), .in_3(in_1), .out_4(out_45), .in_2(in_34));
  Register1x32_main main_12 (.in_1(in_6), .in_3(in_1), .out_4(out_46), .in_2(in_34));
  Register1x32_main main_13 (.in_1(in_23), .in_3(in_1), .out_4(out_47), .in_2(in_34));
  Register1x32_main main_14 (.in_1(in_17), .in_3(in_1), .out_4(out_48), .in_2(in_34));
  Register1x32_main main_15 (.in_1(in_11), .in_3(in_1), .out_4(out_49), .in_2(in_34));
  Register1x32_main main_16 (.in_1(in_5), .in_3(in_1), .out_4(out_50), .in_2(in_34));
  Register1x32_main main_17 (.in_1(in_33), .in_3(in_1), .out_4(out_51), .in_2(in_34));
  Register1x32_main main_18 (.in_1(in_31), .in_3(in_1), .out_4(out_52), .in_2(in_34));
  Register1x32_main main_19 (.in_1(in_29), .in_3(in_1), .out_4(out_53), .in_2(in_34));
  Register1x32_main main_20 (.in_1(in_27), .in_3(in_1), .out_4(out_54), .in_2(in_34));
  Register1x32_main main_21 (.in_1(in_22), .in_3(in_1), .out_4(out_55), .in_2(in_34));
  Register1x32_main main_22 (.in_1(in_16), .in_3(in_1), .out_4(out_56), .in_2(in_34));
  Register1x32_main main_23 (.in_1(in_10), .in_3(in_1), .out_4(out_57), .in_2(in_34));
  Register1x32_main main_24 (.in_1(in_4), .in_3(in_1), .out_4(out_58), .in_2(in_34));
  Register1x32_main main_25 (.in_1(in_32), .in_3(in_1), .out_4(out_59), .in_2(in_34));
  Register1x32_main main_26 (.in_1(in_30), .in_3(in_1), .out_4(out_60), .in_2(in_34));
  Register1x32_main main_27 (.in_1(in_28), .in_3(in_1), .out_4(out_61), .in_2(in_34));
  Register1x32_main main_28 (.in_1(in_26), .in_3(in_1), .out_4(out_62), .in_2(in_34));
  Register1x32_main main_29 (.in_1(in_21), .in_3(in_1), .out_4(out_63), .in_2(in_34));
  Register1x32_main main_30 (.in_1(in_15), .in_3(in_1), .out_4(out_64), .in_2(in_34));
  Register1x32_main main_31 (.in_1(in_9), .in_3(in_1), .out_4(out_65), .in_2(in_34));
  Register1x32_main main_32 (.in_1(in_3), .in_3(in_1), .out_4(out_66), .in_2(in_34));
endmodule
