// Logisim project Test 4x4.circ as structural Verilog: 1 circuit, main circuit main
module main (
  input  [3:0] When_Gets_Lonely,
  input  [3:0] When_Gets_Alive,
  input  [3:0] When_Gets_Overcroweded,
  input  in_4,
  input  in_5,
  input  in_6,
  input  in_7,
  input  in_8,
  input  in_9,
  input  in_10,
  input  in_11,
  input  in_12,
  input  in_13,
  input  in_14,
  input  in_15,
  input  in_16,
  input  in_17,
  input  in_18,
  input  in_19,
  input  Clock,
  input  Clock_Anabler_Stop,
  output out_22,
  output out_23,
  output out_24,
  output out_25,
  output out_26,
  output out_27,
  output out_28,
  output out_29,
  output out_30,
  output out_31,
  output out_32,
  output out_33,
  output out_34,
  output out_35,
  output out_36,
  output out_37
);

  Logika_komurki_koniec_main main_1 (
    .Cell_is_born_when__x(When_Gets_Alive), .in_2(1'b0), .in_3(1'b0), .in_4(out_26), .in_5(out_27),
    .in_7(1'b0), .in_8(1'b0), .in_9(out_23), .in_11(1'b0), .Overcrowded_when__x(When_Gets_Overcroweded),
    .Cell_gets_onely_when___x(When_Gets_Lonely), .OverwritePin(in_4), .Actual_State(out_22), .CLK(Clock),
    .CLK_enabler(Clock_Anabler_Stop));
  Logika_komurki_koniec_main main_2 (
    .Cell_is_born_when__x(When_Gets_Alive), .in_2(1'b0), .in_3(out_22), .in_4(out_27), .in_5(out_30),
    .in_7(out_23), .in_8(1'b0), .in_9(out_31), .in_11(1'b0), .Overcrowded_when__x(When_Gets_Overcroweded),
    .Cell_gets_onely_when___x(When_Gets_Lonely), .OverwritePin(in_8), .Actual_State(out_26), .CLK(Clock),
    .CLK_enabler(Clock_Anabler_Stop));
  Logika_komurki_koniec_main main_3 (
    .Cell_is_born_when__x(When_Gets_Alive), .in_2(out_26), .in_3(1'b0), .in_4(1'b0), .in_5(1'b0),
    .in_7(out_27), .in_8(out_31), .in_9(out_34), .in_11(out_35),
    .Overcrowded_when__x(When_Gets_Overcroweded), .Cell_gets_onely_when___x(When_Gets_Lonely),
    .OverwritePin(in_12), .Actual_State(out_30), .CLK(Clock), .CLK_enabler(Clock_Anabler_Stop));
  Logika_komurki_koniec_main main_4 (
    .Cell_is_born_when__x(When_Gets_Alive), .in_2(out_31), .in_3(1'b0), .in_4(1'b0), .in_5(1'b0),
    .in_7(out_30), .in_8(out_35), .in_9(1'b0), .in_11(1'b0), .Overcrowded_when__x(When_Gets_Overcroweded),
    .Cell_gets_onely_when___x(When_Gets_Lonely), .OverwritePin(in_16), .Actual_State(out_34), .CLK(Clock),
    .CLK_enabler(Clock_Anabler_Stop));
  Logika_komurki_koniec_main main_5 (
    .Cell_is_born_when__x(When_Gets_Alive), .in_2(1'b0), .in_3(out_22), .in_4(out_27), .in_5(out_26),
    .in_7(1'b0), .in_8(out_24), .in_9(out_28), .in_11(1'b0), .Overcrowded_when__x(When_Gets_Overcroweded),
    .Cell_gets_onely_when___x(When_Gets_Lonely), .OverwritePin(in_5), .Actual_State(out_23), .CLK(Clock),
    .CLK_enabler(Clock_Anabler_Stop));
  Logika_komurki_koniec_main main_6 (
    .Cell_is_born_when__x(When_Gets_Alive), .in_2(out_22), .in_3(out_26), .in_4(out_30), .in_5(out_31),
    .in_7(out_23), .in_8(out_24), .in_9(out_28), .in_11(out_32),
    .Overcrowded_when__x(When_Gets_Overcroweded), .Cell_gets_onely_when___x(When_Gets_Lonely),
    .OverwritePin(in_9), .Actual_State(out_27), .CLK(Clock), .CLK_enabler(Clock_Anabler_Stop));
  Logika_komurki_koniec_main main_7 (
    .Cell_is_born_when__x(When_Gets_Alive), .in_2(out_26), .in_3(out_30), .in_4(out_34), .in_5(out_35),
    .in_7(out_27), .in_8(out_28), .in_9(out_32), .in_11(out_36),
    .Overcrowded_when__x(When_Gets_Overcroweded), .Cell_gets_onely_when___x(When_Gets_Lonely),
    .OverwritePin(in_13), .Actual_State(out_31), .CLK(Clock), .CLK_enabler(Clock_Anabler_Stop));
  Logika_komurki_koniec_main main_8 (
    .Cell_is_born_when__x(When_Gets_Alive), .in_2(1'b0), .in_3(1'b0), .in_4(out_30), .in_5(out_34),
    .in_7(out_31), .in_8(out_32), .in_9(out_36), .in_11(1'b0), .Overcrowded_when__x(When_Gets_Overcroweded),
    .Cell_gets_onely_when___x(When_Gets_Lonely), .OverwritePin(in_17), .Actual_State(out_35), .CLK(Clock),
    .CLK_enabler(Clock_Anabler_Stop));
  Logika_komurki_koniec_main main_9 (
    .Cell_is_born_when__x(When_Gets_Alive), .in_2(1'b0), .in_3(out_27), .in_4(out_28), .in_5(out_23),
    .in_7(1'b0), .in_8(1'b0), .in_9(out_25), .in_11(out_29), .Overcrowded_when__x(When_Gets_Overcroweded),
    .Cell_gets_onely_when___x(When_Gets_Lonely), .OverwritePin(in_6), .Actual_State(out_24), .CLK(Clock),
    .CLK_enabler(Clock_Anabler_Stop));
  Logika_komurki_koniec_main main_10 (
    .Cell_is_born_when__x(When_Gets_Alive), .in_2(out_24), .in_3(out_23), .in_4(out_27), .in_5(out_31),
    .in_7(out_25), .in_8(out_29), .in_9(out_32), .in_11(out_33),
    .Overcrowded_when__x(When_Gets_Overcroweded), .Cell_gets_onely_when___x(When_Gets_Lonely),
    .OverwritePin(in_10), .Actual_State(out_28), .CLK(Clock), .CLK_enabler(Clock_Anabler_Stop));
  Logika_komurki_koniec_main main_11 (
    .Cell_is_born_when__x(When_Gets_Alive), .in_2(out_27), .in_3(out_31), .in_4(out_35), .in_5(out_36),
    .in_7(out_28), .in_8(out_29), .in_9(out_33), .in_11(out_37),
    .Overcrowded_when__x(When_Gets_Overcroweded), .Cell_gets_onely_when___x(When_Gets_Lonely),
    .OverwritePin(in_14), .Actual_State(out_32), .CLK(Clock), .CLK_enabler(Clock_Anabler_Stop));
  Logika_komurki_koniec_main main_12 (
    .Cell_is_born_when__x(When_Gets_Alive), .in_2(1'b0), .in_3(out_31), .in_4(1'b0), .in_5(out_35),
    .in_7(out_32), .in_8(1'b0), .in_9(out_37), .in_11(out_33), .Overcrowded_when__x(When_Gets_Overcroweded),
    .Cell_gets_onely_when___x(When_Gets_Lonely), .OverwritePin(in_18), .Actual_State(out_36), .CLK(Clock),
    .CLK_enabler(Clock_Anabler_Stop));
  Logika_komurki_koniec_main main_13 (
    .Cell_is_born_when__x(When_Gets_Alive), .in_2(out_24), .in_3(out_28), .in_4(1'b0), .in_5(1'b0),
    .in_7(1'b0), .in_8(1'b0), .in_9(1'b0), .in_11(out_29), .Overcrowded_when__x(When_Gets_Overcroweded),
    .Cell_gets_onely_when___x(When_Gets_Lonely), .OverwritePin(in_7), .Actual_State(out_25), .CLK(Clock),
    .CLK_enabler(Clock_Anabler_Stop));
  Logika_komurki_koniec_main main_14 (
    .Cell_is_born_when__x(When_Gets_Alive), .in_2(out_24), .in_3(out_28), .in_4(out_32), .in_5(1'b0),
    .in_7(out_25), .in_8(out_33), .in_9(1'b0), .in_11(1'b0), .Overcrowded_when__x(When_Gets_Overcroweded),
    .Cell_gets_onely_when___x(When_Gets_Lonely), .OverwritePin(in_11), .Actual_State(out_29), .CLK(Clock),
    .CLK_enabler(Clock_Anabler_Stop));
  Logika_komurki_koniec_main main_15 (
    .Cell_is_born_when__x(When_Gets_Alive), .in_2(1'b0), .in_3(out_32), .in_4(1'b0), .in_5(out_33),
    .in_7(out_29), .in_8(out_28), .in_9(out_37), .in_11(1'b0), .Overcrowded_when__x(When_Gets_Overcroweded),
    .Cell_gets_onely_when___x(When_Gets_Lonely), .OverwritePin(in_15), .Actual_State(out_33), .CLK(Clock),
    .CLK_enabler(Clock_Anabler_Stop));
  Logika_komurki_koniec_main main_16 (
    .Cell_is_born_when__x(When_Gets_Alive), .in_2(out_33), .in_3(out_32), .in_4(out_36), .in_5(1'b0),
    .in_7(1'b0), .in_8(1'b0), .in_9(1'b0), .in_11(1'b0), .Overcrowded_when__x(When_Gets_Overcroweded),
    .Cell_gets_onely_when___x(When_Gets_Lonely), .OverwritePin(in_19), .Actual_State(out_37), .CLK(Clock),
    .CLK_enabler(Clock_Anabler_Stop));
endmodule
