// Logisim project Uu_Down32.circ as structural Verilog: 1 circuit, main circuit main
module main (
  input  [4:0] in_1,
  input  [31:0] in_2,
  output [31:0] out_3,
  output [31:0] out_4,
  output [31:0] out_5,
  output [31:0] out_6,
  output [31:0] out_7,
  output [31:0] out_8,
  output [31:0] out_9,
  output [31:0] out_10,
  output [31:0] out_11,
  output [31:0] out_12,
  output [31:0] out_13,
  output [31:0] out_14,
  output [31:0] out_15,
  output [31:0] out_16,
  output [31:0] out_17,
  output [31:0] out_18,
  output [31:0] out_19,
  output [31:0] out_20,
  output [31:0] out_21,
  output [31:0] out_22,
  output [31:0] out_23,
  output [31:0] out_24,
  output [31:0] out_25,
  output [31:0] out_26,
  output [31:0] out_27,
  output [31:0] out_28,
  output [31:0] out_29,
  output [31:0] out_30,
  output [31:0] out_31,
  output [31:0] out_32,
  output [31:0] out_33,
  output [31:0] out_34
);

  Uu_Down1_main main_1 (.in_1(in_2), .in_2(in_1), .in_3({5{1'b1}}), .out_4(out_3));
  Uu_Down1_main main_2 (.in_1(in_2), .in_2(in_1), .in_3(5'b11110), .out_4(out_4));
  Uu_Down1_main main_3 (.in_1(in_2), .in_2(in_1), .in_3(5'b11101), .out_4(out_5));
  Uu_Down1_main main_4 (.in_1(in_2), .in_2(in_1), .in_3(5'b11100), .out_4(out_6));
  Uu_Down1_main main_5 (.in_1(in_2), .in_2(in_1), .in_3(5'b11011), .out_4(out_7));
  Uu_Down1_main main_6 (.in_1(in_2), .in_2(in_1), .in_3(5'b11010), .out_4(out_8));
  Uu_Down1_main main_7 (.in_1(in_2), .in_2(in_1), .in_3(5'b11001), .out_4(out_9));
  Uu_Down1_main main_8 (.in_1(in_2), .in_2(in_1), .in_3(5'b11000), .out_4(out_10));
  Uu_Down1_main main_9 (.in_1(in_2), .in_2(in_1), .in_3(5'b10111), .out_4(out_11));
  Uu_Down1_main main_10 (.in_1(in_2), .in_2(in_1), .in_3(5'b10110), .out_4(out_12));
  Uu_Down1_main main_11 (.in_1(in_2), .in_2(in_1), .in_3(5'b10101), .out_4(out_13));
  Uu_Down1_main main_12 (.in_1(in_2), .in_2(in_1), .in_3(5'b10100), .out_4(out_14));
  Uu_Down1_main main_13 (.in_1(in_2), .in_2(in_1), .in_3(5'b10011), .out_4(out_15));
  Uu_Down1_main main_14 (.in_1(in_2), .in_2(in_1), .in_3(5'b10010), .out_4(out_16));
  Uu_Down1_main main_15 (.in_1(in_2), .in_2(in_1), .in_3(5'b10001), .out_4(out_17));
  Uu_Down1_main main_16 (.in_1(in_2), .in_2(in_1), .in_3(5'b10000), .out_4(out_18));
  Uu_Down1_main main_17 (.in_1(in_2), .in_2(in_1), .in_3(5'b01111), .out_4(out_19));
  Uu_Down1_main main_18 (.in_1(in_2), .in_2(in_1), .in_3(5'b01110), .out_4(out_20));
  Uu_Down1_main main_19 (.in_1(in_2), .in_2(in_1), .in_3(5'b01101), .out_4(out_21));
  Uu_Down1_main main_20 (.in_1(in_2), .in_2(in_1), .in_3(5'b01100), .out_4(out_22));
  Uu_Down1_main main_21 (.in_1(in_2), .in_2(in_1), .in_3(5'b01011), .out_4(out_23));
  Uu_Down1_main main_22 (.in_1(in_2), .in_2(in_1), .in_3(5'b01010), .out_4(out_24));
  Uu_Down1_main main_23 (.in_1(in_2), .in_2(in_1), .in_3(5'b01001), .out_4(out_25));
  Uu_Down1_main main_24 (.in_1(in_2), .in_2(in_1), .in_3(5'b01000), .out_4(out_26));
  Uu_Down1_main main_25 (.in_1(in_2), .in_2(in_1), .in_3(5'b00111), .out_4(out_27));
  Uu_Down1_main main_26 (.in_1(in_2), .in_2(in_1), .in_3(5'b00110), .out_4(out_28));
  Uu_Down1_main main_27 (.in_1(in_2), .in_2(in_1), .in_3(5'b00101), .out_4(out_29));
  Uu_Down1_main main_28 (.in_1(in_2), .in_2(in_1), .in_3(5'b00100), .out_4(out_30));
  Uu_Down1_main main_29 (.in_1(in_2), .in_2(in_1), .in_3(5'b00011), .out_4(out_31));
  Uu_Down1_main main_30 (.in_1(in_2), .in_2(in_1), .in_3(5'b00010), .out_4(out_32));
  Uu_Down1_main main_31 (.in_1(in_2), .in_2(in_1), .in_3(5'b00001), .out_4(out_33));
  Uu_Down1_main main_32 (.in_1(in_2), .in_2(in_1), .in_3({5{1'b0}}), .out_4(out_34));
endmodule
